# Fritzing sketch Handwash Robot Electronics (saved by Fritzing 0.9.3b)
breadboards: 1

parts:
  Part1 = Arduino Uno (Rev3)
  Part2 = Bluetooth HC-05 Macho
  J2 = Basic Servo
  J1 = Basic Servo

nets:
  N1: Part1.D8, J1.pulse
  N2: Part1.D9_PWM, J2.pulse
  N3: Part1.D6_PWM, Part2.RXD
  N4: Part1.D7, Part2.TXD
  VCC: Part1.5V, Part2.VCC, J2.vcc, J1.vcc
  GND: Part1.GND, Part2.GND, J2.gnd, J1.gnd
